# Fritzing sketch Foam_Cutter (saved by Fritzing 0.9.6b)
breadboards: 1

parts:
  Mod1 = Raspberry Pi 4B
  Part2 = I2C level shifter bidirectional
  M1 = Stepper Motor - Bipolar
  M2 = Stepper Motor - Bipolar
  VCC1 = Mean Well RD-65B Enclosed Switching AC-to-DC Power Supply, Dual Output, 5V-24V
  Part3 = TB6600 STEPPER MOTOR DRIVER
  Part4 = TB6600 STEPPER MOTOR DRIVER
  Part5 = I2C level shifter bidirectional  # not connected

nets:
  N1: Mod1.3V3, Part2.LV
  N2: Mod1.5V, Part2.HV, VCC1.+V1
  GND: Mod1.GND, Part2.GND, VCC1.Com, Part3.GND, Part3.PUL-, Part3.DIR-, Part3.ENA-, Part4.GND, Part4.PUL-, Part4.DIR-, Part4.ENA-
  N3: Mod1.GPIO22, Part2.LV1
  N4: Mod1.GPIO23, Part2.LV2
  N5: Mod1.GPIO24, Part2.LV3
  N6: Mod1.GPIO25, Part2.LV4
  N7: Part2.HV1, Part3.PUL+
  N8: Part2.HV2, Part3.DIR+
  N9: Part2.HV3, Part4.DIR+
  N10: Part2.HV4, Part4.PUL+
  VCC: M1.A, M2.A, VCC1.+V2, Part3.VCC, Part3.A+, Part3.ENA+, Part4.VCC, Part4.A+, Part4.ENA+
  N11: M1.C, Part3.A-
  N12: M1.B, Part3.B+
  N13: M1.D, Part3.B-
  N14: M2.C, Part4.A-
  N15: M2.B, Part4.B+
  N16: M2.D, Part4.B-

notes:
  ENA+ requires 5V, not motor voltage

custom parts:
  Mean Well RD-65B Enclosed Switching AC-to-DC Power Supply, Dual Output, 5V-24V: Your standard 2x AA battery pack (3 Volts)
