# Fritzing sketch StepperDriverA4988 (saved by Fritzing 0.9.6b)

parts:
  Raspberry_Pi_4B = Raspberry Pi 4B
  Stepper_motor = Stepper Motor - Bipolar
  A4988 = Pololu A4988 [package=SO16]

nets:
  3V3: Raspberry_Pi_4B.3V3, A4988.VDD
  N1: Raspberry_Pi_4B.GND, Raspberry_Pi_4B.GPIO15, A4988.GND#8
  N2: Raspberry_Pi_4B.GPIO27, A4988.MS1
  N3: Raspberry_Pi_4B.GPIO23, A4988.MS2
  N4: Raspberry_Pi_4B.GPIO24, A4988.MS3
  N5: Raspberry_Pi_4B.GPIO25, A4988.STEP
  N6: Raspberry_Pi_4B.GPIO5, A4988.DIR
  N7: Stepper_motor.A, A4988.2B
  N8: Stepper_motor.C, A4988.2A
  N9: Stepper_motor.B, A4988.1A
  N10: Stepper_motor.D, A4988.1B
  N11: A4988.RESET, A4988.SLEEP

notes:
  5.1 VDC, 3 Amps
  AC converter
  24 VDC, 5 Amps
  bench supply
  3.3 VDC provided by RaspPi
